# Fritzing sketch esp-fc-esp32-i2c (saved by Fritzing 0.9.6b)
circuit board: 7.68022cm x 4.37895cm
breadboards: 1

parts:
  MPU-6050 = IMU Digital Combo Board 6DOF
  J1 = Dagu DGServo 9g header (male) [package=THT]
  J2 = Dagu DGServo 9g header (male) [package=THT]
  J3 = Dagu DGServo 9g header (male) [package=THT]
  J4 = Dagu DGServo 9g header (male) [package=THT]
  J5 = Dagu DGServo 9g header (male) [package=THT]
  J6 = Dagu DGServo 9g header (male) [package=THT]
  Openlog = OpenLog
  J7 = Dagu DGServo 9g header connector (female) [package=THT]
  PNP = PNP-Transistor [package="TO92 [THT]"]
  R1 = Resistor [tolerance=±5% resistance=2.2k power=0.25 package=THT]
  R3 = Resistor [tolerance=±5% resistance=22k power=0.25 package=THT]
  R2 = Resistor [tolerance=±5% resistance=3.3k power=0.25 package=THT]
  J8 = female pin header, 2 pins [form="♀ (female)"]
  J9 = Piezo Speaker
  C4 = Ceramic Capacitor [capacitance=100nF package="100 mil [THT, multilayer]"]
  C5 = Electrolytic Capacitor [capacitance=47µF voltage=35V package="100 mil [THT, electrolytic]"]
  MH-ET_Live_Minikit_for_ESP1 = MH-ET Live Minikit for ESP32
  C3 = Ceramic Capacitor [capacitance=100nF voltage=35V package="100 mil [THT, multilayer]"]

nets:
  3.3V: MPU-6050.3.3V, MH-ET_Live_Minikit_for_ESP1.3.3V, C3.1
  GND: MPU-6050.GND, J1.gnd, J2.gnd, J3.gnd, J4.gnd, J5.gnd, J6.gnd, PNP.C, R2.Pin_0, J8.pin1, C4.0, C5.-, MH-ET_Live_Minikit_for_ESP1.GND, C3.0
  N1: MPU-6050.SDA, MH-ET_Live_Minikit_for_ESP1.IO21
  N2: MPU-6050.SCL, MH-ET_Live_Minikit_for_ESP1.IO22
  5V: J1.Vcc, J2.Vcc, J3.Vcc, J4.Vcc, J5.Vcc, J6.Vcc, J9.pin2, C4.1, C5.+, MH-ET_Live_Minikit_for_ESP1.VCC
  N3: J1.pulse, MH-ET_Live_Minikit_for_ESP1.IO33
  N4: J2.pulse, MH-ET_Live_Minikit_for_ESP1.IO16
  N5: J3.pulse, MH-ET_Live_Minikit_for_ESP1.TDI
  N6: J4.pulse, MH-ET_Live_Minikit_for_ESP1.IO4
  N7: J5.pulse, MH-ET_Live_Minikit_for_ESP1.IO25
  N8: J6.pulse, MH-ET_Live_Minikit_for_ESP1.IO27
  N9: Openlog.RXI, J7.pulse
  VCC: Openlog.VCC, J7.Vcc
  GND_2: Openlog.GND, J7.gnd
  N10: PNP.E, J9.pin1
  N11: PNP.B, R1.Pin_0
  N12: R1.Pin_1, MH-ET_Live_Minikit_for_ESP1.IO0
  N13: R3.Pin_0, J8.pin2
  N14: R3.Pin_1, R2.Pin_1, MH-ET_Live_Minikit_for_ESP1.SVP

notes:
  TX2 BBL
  RX3 RX
  PMW3
  PWM4
  PWM2
  PWM1
  VBAT
  5V

custom parts:
  MH-ET Live Minikit for ESP32: MH-ET Live Minikit for ESP32 ( http://mh.nodebb.com/topic/8/mh-et-live-minikit-for-esp32/2/) PCB footprint is invalid.
