# Fritzing sketch esp-fc-esp32-spi (saved by Fritzing 0.9.6b)
circuit board: 7.68022cm x 4.37895cm
breadboards: 1

parts:
  J1 = Dagu DGServo 9g header (male) [package=THT]
  J2 = Dagu DGServo 9g header (male) [package=THT]
  J3 = Dagu DGServo 9g header (male) [package=THT]
  J4 = Dagu DGServo 9g header (male) [package=THT]
  J5 = Dagu DGServo 9g header (male) [package=THT]
  J6 = Dagu DGServo 9g header (male) [package=THT]
  Openlog = OpenLog
  J7 = Dagu DGServo 9g header connector (female) [package=THT]
  PNP = PNP-Transistor [package="TO92 [THT]"]
  R1 = Resistor [tolerance=±5% resistance=2.2k power=0.25 package=THT]
  R3 = Resistor [tolerance=±5% resistance=22k power=0.25 package=THT]
  R2 = Resistor [tolerance=±5% resistance=3.3k power=0.25 package=THT]
  J8 = female pin header, 2 pins [form="♀ (female)"]
  J9 = Piezo Speaker
  C4 = Ceramic Capacitor [capacitance=100nF package="100 mil [THT, multilayer]"]
  C5 = Electrolytic Capacitor [capacitance=47µF voltage=35V package="100 mil [THT, electrolytic]"]
  MH-ET_Live_Minikit_for_ESP1 = MH-ET Live Minikit for ESP32
  C3 = Ceramic Capacitor [capacitance=100nF voltage=35V package="100 mil [THT, multilayer]"]
  M1 = gy9250

nets:
  GND: J1.gnd, J2.gnd, J3.gnd, J4.gnd, J5.gnd, J6.gnd, PNP.C, R2.Pin_0, J8.pin1, C4.0, C5.-, MH-ET_Live_Minikit_for_ESP1.GND, C3.0, M1.pin2
  5V: J1.Vcc, J2.Vcc, J3.Vcc, J4.Vcc, J5.Vcc, J6.Vcc, J9.pin2, C4.1, C5.+, MH-ET_Live_Minikit_for_ESP1.VCC
  N1: J1.pulse, MH-ET_Live_Minikit_for_ESP1.IO33
  N2: J2.pulse, MH-ET_Live_Minikit_for_ESP1.IO16
  N3: J3.pulse, MH-ET_Live_Minikit_for_ESP1.TDI
  N4: J4.pulse, MH-ET_Live_Minikit_for_ESP1.IO4
  N5: J5.pulse, MH-ET_Live_Minikit_for_ESP1.IO25
  N6: J6.pulse, MH-ET_Live_Minikit_for_ESP1.IO27
  N7: Openlog.RXI, J7.pulse
  VCC: Openlog.VCC, J7.Vcc
  GND_2: Openlog.GND, J7.gnd
  N8: PNP.E, J9.pin1
  N9: PNP.B, R1.Pin_0
  N10: R1.Pin_1, MH-ET_Live_Minikit_for_ESP1.IO0
  N11: R3.Pin_0, J8.pin2
  N12: R3.Pin_1, R2.Pin_1, MH-ET_Live_Minikit_for_ESP1.SVP
  N13: MH-ET_Live_Minikit_for_ESP1.IO18, M1.pin3
  N14: MH-ET_Live_Minikit_for_ESP1.IO19, M1.pin7
  N15: MH-ET_Live_Minikit_for_ESP1.IO23, M1.pin4
  N16: MH-ET_Live_Minikit_for_ESP1.IO5, M1.pin9
  N17: MH-ET_Live_Minikit_for_ESP1.3.3V, M1.pin1

notes:
  TX2 BBL
  RX3 RX
  PMW3
  PWM4
  PWM2
  PWM1
  VBAT
  5V

custom parts:
  MH-ET Live Minikit for ESP32: MH-ET Live Minikit for ESP32 ( http://mh.nodebb.com/topic/8/mh-et-live-minikit-for-esp32/2/) PCB footprint is invalid.
  gy9250: MPU-9250 module (three-axis gyroscope + three-axis acceleration + three-axis magnetic field). The generic model from ebay et. al. rather than the Sparkfun version.
