# Fritzing sketch esp-fc-esp8266-i2c (saved by Fritzing 0.9.3b)
circuit board: 7.23026cm x 4.0855cm
breadboards: 1

parts:
  WeMos_D1_Mini1 = WeMos D1 Mini
  MPU-6050 = IMU Digital Combo Board 6DOF
  J1 = Dagu DGServo 9g header (male) [package=THT]
  J2 = Dagu DGServo 9g header (male) [package=THT]
  J3 = Dagu DGServo 9g header (male) [package=THT]
  J4 = Dagu DGServo 9g header (male) [package=THT]
  J5 = Dagu DGServo 9g header (male) [package=THT]
  J6 = Dagu DGServo 9g header (male) [package=THT]
  Openlog = OpenLog
  J7 = Dagu DGServo 9g header connector (female) [package=THT]
  PNP = PNP-Transistor [package="TO92 [THT]"]
  R1 = Resistor [tolerance=±5% resistance=2.2k package=THT]
  D1 = Rectifier Diode [part_number=1N4001 package="300 mil [THT]"]
  R3 = Resistor [tolerance=±5% resistance=22k package=THT]
  R2 = Resistor [tolerance=±5% resistance=4.7k package=THT]
  J8 = female pin header, 2 pins [form="♀ (female)"]
  J9 = Piezo Speaker
  C3 = Ceramic Capacitor [capacitance=100nF package="100 mil [THT, multilayer]"]
  C4 = Ceramic Capacitor [capacitance=100nF package="100 mil [THT, multilayer]"]
  C5 = Electrolytic Capacitor [capacitance=47µF package="100 mil [THT, electrolytic]"]

nets:
  3V3: WeMos_D1_Mini1.3V3, MPU-6050.3.3V, C3.1
  5V: WeMos_D1_Mini1.5V, J1.Vcc, J2.Vcc, J3.Vcc, J4.Vcc, J5.Vcc, J6.Vcc, J9.pin2, C4.1, C5.+
  N1: WeMos_D1_Mini1.A0, R3.Pin_1, R2.Pin_1
  N2: WeMos_D1_Mini1.D0, R1.Pin_1
  N3: WeMos_D1_Mini1.D1, MPU-6050.SCL
  N4: WeMos_D1_Mini1.D2, MPU-6050.SDA
  N5: WeMos_D1_Mini1.D3, J3.pulse
  N6: WeMos_D1_Mini1.D4, J1.pulse
  N7: WeMos_D1_Mini1.D5, J4.pulse
  N8: WeMos_D1_Mini1.D6, J5.pulse
  N9: WeMos_D1_Mini1.D7, J2.pulse
  N10: WeMos_D1_Mini1.D8, J6.pulse
  GND: WeMos_D1_Mini1.G, MPU-6050.GND, J1.gnd, J2.gnd, J3.gnd, J4.gnd, J5.gnd, J6.gnd, PNP.C, R2.Pin_0, J8.pin1, C3.0, C4.0, C5.-
  N11: Openlog.RXI, J7.pulse
  VCC: Openlog.VCC, J7.Vcc
  GND_2: Openlog.GND, J7.gnd
  N12: PNP.E, J9.pin1
  N13: PNP.B, R1.Pin_0
  N14: D1.cathode, R3.Pin_0
  N15: D1.anode, J8.pin2

notes:
  D0 - Buzzer
  D1 - I2C, SCL
  D2 - I2C, SDA
  D3 - PWM1
  D4 - TX2, Blackbox
  D5 - PMW2
  D6 - PWM3
  D7 - RX-PPM
  D8 - PWM4
  A0 - ADC
  Blackbox
  RX-PPM
  PMW1
  PWM2
  PWM3
  PWM4
