# Fritzing sketch espfc_wemos_mini32 (saved by Fritzing 0.9.4)

parts:
  MH-ET_Live_Minikit_for_ESP1 = MH-ET Live Minikit for ESP32
  M1 = gy9250
  J11 = Dagu DGServo 9g header (male) [package=THT]
  J16 = Dagu DGServo 9g header (male) [package=THT]
  J17 = Dagu DGServo 9g header (male) [package=THT]
  J18 = Dagu DGServo 9g header (male) [package=THT]
  J19 = Dagu DGServo 9g header (male) [package=THT]
  J14 = Dagu DGServo 9g header (male) [package=THT]
  J8 = Dagu DGServo 9g header (male) [package=THT]

nets:
  N1: MH-ET_Live_Minikit_for_ESP1.GND, M1.pin2
  N2: MH-ET_Live_Minikit_for_ESP1.SVN, J16.Vcc
  N3: MH-ET_Live_Minikit_for_ESP1.IO35, J18.gnd
  N4: MH-ET_Live_Minikit_for_ESP1.IO33, J18.Vcc
  N5: MH-ET_Live_Minikit_for_ESP1.TMS, J8.gnd
  N6: MH-ET_Live_Minikit_for_ESP1.CMD, M1.pin10
  N7: MH-ET_Live_Minikit_for_ESP1.SVP, J16.pulse
  N8: MH-ET_Live_Minikit_for_ESP1.IO26, J11.pulse
  N9: MH-ET_Live_Minikit_for_ESP1.IO18, M1.pin3
  N10: MH-ET_Live_Minikit_for_ESP1.IO19, M1.pin5
  N11: MH-ET_Live_Minikit_for_ESP1.IO23, M1.pin4
  N12: MH-ET_Live_Minikit_for_ESP1.IO5, M1.pin9
  N13: MH-ET_Live_Minikit_for_ESP1.3.3V, M1.pin1
  N14: MH-ET_Live_Minikit_for_ESP1.TCK, J8.Vcc
  N15: MH-ET_Live_Minikit_for_ESP1.IO22, J19.Vcc
  N16: MH-ET_Live_Minikit_for_ESP1.IO21, J19.gnd
  N17: MH-ET_Live_Minikit_for_ESP1.IO17, J17.gnd
  N18: MH-ET_Live_Minikit_for_ESP1.IO16, J17.Vcc
  N19: MH-ET_Live_Minikit_for_ESP1.IO27, J11.gnd
  N20: MH-ET_Live_Minikit_for_ESP1.IO25, J14.gnd
  N21: MH-ET_Live_Minikit_for_ESP1.IO32, J18.pulse
  N22: MH-ET_Live_Minikit_for_ESP1.TDI, J8.pulse
  N23: MH-ET_Live_Minikit_for_ESP1.IO4, J19.pulse
  N24: MH-ET_Live_Minikit_for_ESP1.IO0, J14.pulse
  N25: MH-ET_Live_Minikit_for_ESP1.IO2, J14.Vcc

notes:
  M7
  M6
  M5
  M4
  -
  M3
  M2
  M1
  M0
  Voltage
  Current
  -
  PPM
  TX1
  RX1
  -
  TX2
  RX2
  I2C/SCL
  I2C/SDA
  BUZZER

custom parts:
  MH-ET Live Minikit for ESP32: MH-ET Live Minikit for ESP32 ( http://mh.nodebb.com/topic/8/mh-et-live-minikit-for-esp32/2/) PCB footprint is invalid.
  gy9250: MPU-9250 module (three-axis gyroscope + three-axis acceleration + three-axis magnetic field). The generic model from ebay et. al. rather than the Sparkfun version.
